# Fritzing sketch Fritzing Sketch Source File (saved by Fritzing 0.9.3b)
breadboards: 1

parts:
  Part1 = Arduino Uno (Rev3)
  J1 = Basic Servo
  J2 = Basic Servo
  Part2 = Thumb Joystick

nets:
  N1: Part1.A0, Part2.VERT
  N2: Part1.A1, Part2.HORZ
  N3: Part1.D3_PWM, J1.pulse
  N4: Part1.D5_PWM, J2.pulse
  VCC: Part1.5V, J1.vcc, J2.vcc, Part2.VCC
  GND: Part1.GND, J1.gnd, J2.gnd, Part2.GND

notes:
  GND - Green
  5VC - Red
  GPIO - Blue
  Developed By Web Dev Fusion
  www.webdevfusion.com
  Developed By Web Dev Fusion
  https://www.webdevfusion.com
